# Fritzing sketch Multisensor (saved by Fritzing 0.9.2b)
breadboards: 1

parts:
  Part1 = Arduino Nano (Rev3.0) (ICSP)
  DHT1 = DHT22 Humidity and Temperature Sensor
  R2 = Resistor [tolerance=±5% resistance=10k package="0402 [SMD]"]
  R3 = PHOTOCELL [package=photocell]
  R4 = Resistor [tolerance=±5% resistance=10k package="0402 [SMD]"]
  PIR1 = PIR sensor

nets:
  GND: Part1.GND, DHT1.GND, R4.Pin_0, PIR1.GND
  N1: Part1.D3, PIR1.SIG
  N2: Part1.D6, DHT1.DATA, R2.Pin_1
  VDD: Part1.5V, DHT1.VDD, R2.Pin_0, R3.P$2, PIR1.VDD
  N3: Part1.A0, R3.P$1, R4.Pin_1
